# Fritzing sketch sreg-daisy (saved by Fritzing 0.9.3b)
breadboards: 1

parts:
  U1 = 74HC595 [package="DIP16 [THT]"]
  Part1 = Arduino Uno (Rev3)
  U2 = 74HC595 [package="DIP16 [THT]"]

nets:
  GND: U1.GND, U2.GND
  N1: U1.Q7', U2.DS
  VCC: U1.MR, U1.VCC, Part1.5V, U2.MR, U2.VCC
  N2: U1.SH_CP, Part1.D3_PWM, U2.SH_CP
  N3: U1.ST_CP, Part1.D4, U2.ST_CP
  N4: U1.OE, Part1.GND, U2.OE
  N5: U1.DS, Part1.D2
